# Fritzing sketch schematic (saved by Fritzing 0.9.3b)
breadboards: 1

parts:
  RTC = Real Time Clock Module - DS1307 RTC Breakout Board
  LED1 = LED - 3mm [color="Red (633nm)" package="3 mm [THT]"]
  LED2 = LED - 3mm [color="Blue (430nm)" package="3 mm [THT]"]
  MINUS_SW = Pushbutton [package="[THT]"]
  Clock_display = Grove 4 Digit Display
  R1 = Resistor [tolerance=±5% resistance=470 package=THT]
  R2 = Resistor [tolerance=±5% resistance=220 package=THT]
  Part4 = Arduino Nano (Rev3.0) (ICSP)
  R3 = Resistor [tolerance=±5% resistance=4.7k package=THT]
  MODE_SW = Pushbutton [package="[THT]"]
  PLUS_SW = Pushbutton [package="[THT]"]

nets:
  5V: RTC.5V, Clock_display.VCC, Part4.5V, R3.Pin_0
  GND: RTC.GND, LED1.cathode, LED2.cathode, MINUS_SW.Pin_1, MINUS_SW.Pin_2, Clock_display.GND, Part4.GND, MODE_SW.Pin_1, MODE_SW.Pin_2, PLUS_SW.Pin_1, PLUS_SW.Pin_2
  N1: RTC.SQW, Part4.D2, R3.Pin_1
  N2: RTC.SCL, Part4.A5
  N3: RTC.SDA, Part4.A4
  N4: LED1.anode, R2.Pin_1
  N5: LED2.anode, R1.Pin_1
  N6: MINUS_SW.Pin_3, MINUS_SW.Pin_4, Part4.D9
  N7: Clock_display.DIO, Part4.D12/MISO
  N8: Clock_display.CLK, Part4.D11/MOSI
  N9: R1.Pin_0, Part4.D5
  N10: R2.Pin_0, Part4.D6
  N11: Part4.D8, MODE_SW.Pin_3, MODE_SW.Pin_4
  N12: Part4.D10, PLUS_SW.Pin_3, PLUS_SW.Pin_4
